// Logisim project Main_and_ALU_Decoder.circ as structural Verilog
module ALUDecoder (
  input  ALUOp,
  input  [4:0] Funct_0_5,
  output [1:0] ALUControl,
  output [1:0] FlagW
);

  wire and_1_out, and_2_out, and_3_out;
  wire [1:0] or_1_out;

  and and_1 (and_1_out, ~Funct_0_5[1], Funct_0_5[2], ~Funct_0_5[3], ~Funct_0_5[4]);  // AND_Gate
  and and_2 (and_2_out, ~Funct_0_5[1], ~Funct_0_5[2], Funct_0_5[3], Funct_0_5[4]);  // AND_Gate
  and and_3 (and_3_out, ~Funct_0_5[1], ~Funct_0_5[2], ~Funct_0_5[3], ~Funct_0_5[4]);  // AND_Gate
  or or_1 (or_1_out[0], and_1_out, and_2_out);
  or or_2 (or_1_out[1], and_2_out, and_3_out);
  Multiplexer #(.width(2), .enable("false")) multiplexer_1 (.in0(2'b00), .in1(or_1_out), .out(ALUControl), .sel(ALUOp));
  and and_4 (FlagW[0], Funct_0_5[0], ~or_1_out[0]);  // AND_Gate

  assign FlagW[1] = Funct_0_5[0];
endmodule

module MainDecoder (
  input  [31:0] in_1,
  output Branch,
  output MemToReg,
  output MemW,
  output ALUSrc,
  output [1:0] ImmSrc,
  output RegW,
  output [1:0] RegSrc,
  output ALUOP
);

  wire and_3_out, and_4_out, and_5_out, and_7_out, and_8_out, multiplexer_1_out, not_1_out, xor_1_out;

  Multiplexer #(.select(2), .enable("false")) multiplexer_1 (
    .in0(1'b0), .in1(1'b1), .in2(1'b0), .out(multiplexer_1_out), .sel(in_1[27:26]));  // open: in3
  Multiplexer #(.select(2), .enable("false")) multiplexer_2 (
    .in0(1'b0), .in1(1'b1), .in2(1'b0), .in3(1'b0), .out(Branch), .sel(in_1[27:26]));
  and and_1 (MemToReg, multiplexer_1_out, in_1[20]);
  and and_2 (MemW, multiplexer_1_out, ~in_1[20]);  // AND_Gate
  xor xor_1 (xor_1_out, in_1[26], in_1[27]);
  and and_3 (and_3_out, ~xor_1_out, in_1[25]);  // AND_Gate
  and and_4 (and_4_out, ~in_1[26], ~in_1[27]);  // AND_Gate
  and and_5 (and_5_out, in_1[26], ~in_1[27], in_1[20]);  // AND_Gate
  and and_6 (RegSrc[0], ~in_1[26], in_1[27]);  // AND_Gate
  and and_7 (and_7_out, ~in_1[26], ~in_1[27], ~in_1[25]);  // AND_Gate
  and and_8 (and_8_out, ~in_1[26], in_1[27], ~in_1[20]);  // AND_Gate
  or or_1 (ALUSrc, xor_1_out, and_3_out);
  not not_1 (not_1_out, and_7_out);
  Multiplexer #(.select(2), .enable("false")) multiplexer_3 (
    .in0(1'b1), .in1(1'b0), .in2(1'b0), .in3(1'b0), .out(ALUOP), .sel(in_1[27:26]));
  Multiplexer #(.width(2)) multiplexer_4 (.in0(in_1[27:26]), .out(ImmSrc), .sel(1'b0), .en(ALUSrc));  // open: in1
  or or_2 (RegW, and_4_out, and_5_out);
  or or_3 (RegSrc[1], not_1_out, and_8_out);
endmodule
