// Logisim project control_unit.circ as structural Verilog
module main (
  input  clk,
  input  [3:0] Rd3_0,
  input  [1:0] Op,
  input  [5:0] Funct5_0,
  input  [3:0] Cond3_0,
  input  [3:0] ALUFlags3_0,
  output PCSrc,
  output RegWrite,
  output MemtoReg,
  output MemWrite,
  output ALUSrc,
  output [1:0] ImmSrc1_0,
  output [1:0] RegSrc1_0,
  output [1:0] ALUControl1_0
);

  wire condition_check_1_condex, main_1_aluop, main_1_branch, memwt, pc_logic_1_pcs, regwt;
  wire [1:0] alu_decoder_1_flagw, and_1_out, bit_extender_1_out, register_1_q, register_2_q;

  pc_logic pc_logic_1 (.Rd_3_0(Rd3_0), .RegWrite(regwt), .Branch(main_1_branch), .PCS(pc_logic_1_pcs));
  main_decoder_main main_1 (
    .op(Op), .f0(Funct5_0[0]), .f5(Funct5_0[5]), .Branch(main_1_branch), .MemtoReg(MemtoReg), .MemW(memwt),
    .ALUSrc(ALUSrc), .ImmSrc(ImmSrc1_0), .RegW(regwt), .RegSrc(RegSrc1_0), .ALUOp(main_1_aluop));
  alu_decoder alu_decoder_1 (
    .Funct_4_0(Funct5_0[4:0]), .ALUOp(main_1_aluop), .FlagW(alu_decoder_1_flagw), .ALUControl(ALUControl1_0));
  Register #(.width(2)) register_1 (.D(ALUFlags3_0[3:2]), .en(and_1_out[1]), .Q(register_1_q), .clk(clk));  // open: clr
  Register #(.width(2)) register_2 (.D(ALUFlags3_0[1:0]), .en(and_1_out[0]), .Q(register_2_q), .clk(clk));  // open: clr
  assign and_1_out = alu_decoder_1_flagw & bit_extender_1_out;  // AND_Gate and_1, 2 bits wide
  assign bit_extender_1_out = {{1{condition_check_1_condex}}, condition_check_1_condex};  // Bit_Extender bit_extender_1
  condition_check condition_check_1 (
    .Flags3_2(register_1_q), .Flags1_0(register_2_q), .Cond_3_0(Cond3_0), .CondEx(condition_check_1_condex));
  and and_2 (PCSrc, pc_logic_1_pcs, condition_check_1_condex);
  and and_3 (RegWrite, regwt, condition_check_1_condex);
  and and_4 (MemWrite, memwt, condition_check_1_condex);

  // Other names for the same wires on the sheet: clkt = clk
endmodule

module alu_decoder (
  input  [4:0] Funct_4_0,
  input  ALUOp,
  output [1:0] FlagW,
  output [1:0] ALUControl
);

  wire [1:0] flag_decoder_1_flag_w_1_0, funct_encoder_1_alucontrol;

  funct_encoder funct_encoder_1 (.funct_4_1(Funct_4_0[4:1]), .ALUControl(funct_encoder_1_alucontrol));
  Multiplexer #(.width(2), .enable("false")) multiplexer_1 (
    .in0(2'b00), .in1(funct_encoder_1_alucontrol), .out(ALUControl), .sel(ALUOp));
  flag_decoder flag_decoder_1 (.ALUControl(ALUControl), .funct0(Funct_4_0[0]), .Flag_W_1_0(flag_decoder_1_flag_w_1_0));
  Multiplexer #(.width(2), .enable("false")) multiplexer_2 (
    .in0(ALUControl), .in1(flag_decoder_1_flag_w_1_0), .out(FlagW), .sel(ALUOp));
endmodule

module funct_encoder (
  input  [3:0] funct_4_1,
  output [1:0] ALUControl
);

  wire and_1_out, and_2_out, and_3_out, and_4_out;

  and and_1 (and_1_out, ~funct_4_1[0], ~funct_4_1[1], ~funct_4_1[2], ~funct_4_1[3]);  // AND_Gate
  or or_1 (ALUControl[1], and_1_out, and_2_out);
  and and_2 (and_2_out, ~funct_4_1[0], ~funct_4_1[1], funct_4_1[2], funct_4_1[3]);  // AND_Gate
  and and_3 (and_3_out, ~funct_4_1[0], funct_4_1[1], ~funct_4_1[2], ~funct_4_1[3]);  // AND_Gate
  or or_2 (ALUControl[0], and_3_out, and_4_out);
  and and_4 (and_4_out, ~funct_4_1[0], ~funct_4_1[1], funct_4_1[2], funct_4_1[3]);  // AND_Gate
endmodule

module flag_decoder (
  input  [1:0] ALUControl,
  input  funct0,
  output [1:0] Flag_W_1_0
);

  and and_1 (Flag_W_1_0[0], funct0, ~ALUControl[1]);  // AND_Gate

  assign Flag_W_1_0[1] = funct0;
endmodule

module pc_logic (
  input  [3:0] Rd_3_0,
  input  RegWrite,
  input  Branch,
  output PCS
);

  wire and_1_out, comparator_1_eq;

  Comparator #(.width(4)) comparator_1 (.a(Rd_3_0), .b(4'b1111), .eq(comparator_1_eq));  // open: gt, lt
  and and_1 (and_1_out, comparator_1_eq, RegWrite);
  or or_1 (PCS, and_1_out, Branch);
endmodule

module conditional_logic (
  input  PCS,
  input  RegW,
  input  MemW,
  input  [1:0] FlagW1_0,
  output PCSrc,
  output RegWrite,
  output MemWrite
);
endmodule

module condition_check (
  input  [1:0] Flags3_2,
  input  [1:0] Flags1_0,
  input  [3:0] Cond_3_0,
  output CondEx
);

  wire and_1_out, not_1_out, xor_1_out;

  not not_1 (not_1_out, Flags3_2[0]);
  xor xor_1 (xor_1_out, Flags3_2[1], Flags1_0[1]);
  and and_1 (and_1_out, ~xor_1_out, not_1_out);  // AND_Gate
  Multiplexer #(.select(4)) multiplexer_1 (
    .in0(Flags3_2[0]), .in1(not_1_out), .in11(xor_1_out), .in12(and_1_out), .in14(1'b1), .out(CondEx),
    .sel(Cond_3_0));  // open: in2, in3, in4, in5, in6, in7, in8, in9, in10, in13, in15, en

  // Notes on the sheet:
  //   N: 10
  //   Z: 01
  //   C:10
  //   V:01
  //   Z
  //   C
  //   EQ Z
  //   NE NOTZ
  //   N
  //   V
  //   LT  N XOR V
  //   GT  Not(Z)Not(NxorV)
  //   AL Always/Uncond
  //    0000 = EQ
  //    0001 = NE
  //    1011 = LT
  //    1100 = GT
  //    1110 = AL
endmodule
