// Logisim project cpu.circ as structural Verilog: 1 circuit, main circuit main
module main (
);

  // RegisterFile registerfile_1: pin names not known
  // control_unit_main main_1: pin names not known
  // ALU alu_1: pin names not known
endmodule
