// Logisim project ALU.circ as structural Verilog: 1 circuit, main circuit ALU
module ALU (
  input  [31:0] A,
  input  [31:0] B,
  input  [1:0] ALUControl,
  output [31:0] ALU_Result,
  output [3:0] ALU_Flags
);

  wire adder_1_cout, and_3_out, and_5_out, not_1_out, not_2_out, or_2_out, subtractor_1_bout, xnor_1_out,
       xor_1_out;
  wire [31:0] adder_1_out, and_1_out, or_1_out, subtractor_1_out;

  Adder #(.width(32)) adder_1 (.a(B), .b(A), .out(adder_1_out), .cout(adder_1_cout));  // open: cin
  Subtractor #(.width(32)) subtractor_1 (.a(A), .b(B), .out(subtractor_1_out), .bout(subtractor_1_bout));  // open: bin
  assign and_1_out = B & A;  // AND_Gate and_1, 32 bits wide
  assign or_1_out = B | A;  // OR_Gate or_1, 32 bits wide
  Multiplexer #(.select(2), .width(32), .enable("false")) multiplexer_1 (
    .in0(adder_1_out), .in1(subtractor_1_out), .in2(and_1_out), .in3(or_1_out),
    .out({ALU_Flags[3], ALU_Result[30:0]}), .sel(ALUControl));
  Comparator #(.width(32)) comparator_1 (
    .a({ALU_Flags[3], ALU_Result[30:0]}), .b({32{1'b0}}), .eq(ALU_Flags[2]));  // open: gt, lt
  NotExactlyOne xnor_1 (.out(xnor_1_out), .in0(A[31]), .in1(B[31]), .in2(ALUControl[0]));
  not not_1 (not_1_out, ALUControl[1]);
  xor xor_1 (xor_1_out, B[31], adder_1_out[31]);
  and and_2 (ALU_Flags[1], xnor_1_out, xor_1_out, not_1_out);
  not not_2 (not_2_out, ALUControl[0]);
  and and_3 (and_3_out, ALUControl[0], subtractor_1_bout);
  or or_2 (or_2_out, and_3_out, and_5_out);
  and and_4 (ALU_Flags[0], not_1_out, or_2_out);
  and and_5 (and_5_out, not_2_out, adder_1_cout);

  assign ALU_Result[31] = ALU_Flags[3];

  // Other names for the same wires on the sheet: C = ALU_Flags[0]; V = ALU_Flags[1]; Z = ALU_Flags[2];
  //   N = ALU_Flags[3]; ALU_Control_0 = ALUControl[0]; ALU_Control_1 = ALUControl[1]
endmodule
