// Logisim project RegisterFile.circ as structural Verilog: 1 circuit, main circuit RegisterFile
module RegisterFile (
  input  [31:0] WD3,
  input  clk,
  input  clr,
  input  [3:0] A1,
  input  [3:0] A2,
  input  [31:0] R15,
  input  WE3,
  input  [3:0] A3,
  output [31:0] RD1,
  output [31:0] RD2
);

  wire decoder_1_out0, decoder_1_out1, decoder_1_out2, decoder_1_out3, decoder_1_out4, decoder_1_out5,
       decoder_1_out6, decoder_1_out7, decoder_1_out8, decoder_1_out9, decoder_1_out10, decoder_1_out11,
       decoder_1_out12, decoder_1_out13, decoder_1_out14;
  wire [31:0] R0_q, R1_q, R2_q, R3_q, R4_q, R5_q, R6_q, R7_q, R8_q, R9_q, R10_q, R11_q, R12_q, R13_q, R14_q;

  Decoder #(.select(4), .disabled(0)) decoder_1 (
    .out0(decoder_1_out0), .out1(decoder_1_out1), .out2(decoder_1_out2), .out3(decoder_1_out3),
    .out4(decoder_1_out4), .out5(decoder_1_out5), .out6(decoder_1_out6), .out7(decoder_1_out7),
    .out8(decoder_1_out8), .out9(decoder_1_out9), .out10(decoder_1_out10), .out11(decoder_1_out11),
    .out12(decoder_1_out12), .out13(decoder_1_out13), .out14(decoder_1_out14), .sel(A3), .en(WE3));  // open: out15
  Register #(.width(32)) R14 (.D(WD3), .en(decoder_1_out14), .Q(R14_q), .clk(clk), .clr(clr));
  Register #(.width(32)) R13 (.D(WD3), .en(decoder_1_out13), .Q(R13_q), .clk(clk), .clr(clr));
  Register #(.width(32)) R12 (.D(WD3), .en(decoder_1_out12), .Q(R12_q), .clk(clk), .clr(clr));
  Register #(.width(32)) R11 (.D(WD3), .en(decoder_1_out11), .Q(R11_q), .clk(clk), .clr(clr));
  Register #(.width(32)) R10 (.D(WD3), .en(decoder_1_out10), .Q(R10_q), .clk(clk), .clr(clr));
  Register #(.width(32)) R9 (.D(WD3), .en(decoder_1_out9), .Q(R9_q), .clk(clk), .clr(clr));
  Register #(.width(32)) R7 (.D(WD3), .en(decoder_1_out7), .Q(R7_q), .clk(clk), .clr(clr));
  Register #(.width(32)) R8 (.D(WD3), .en(decoder_1_out8), .Q(R8_q), .clk(clk), .clr(clr));
  Register #(.width(32)) R6 (.D(WD3), .en(decoder_1_out6), .Q(R6_q), .clk(clk), .clr(clr));
  Register #(.width(32)) R5 (.D(WD3), .en(decoder_1_out5), .Q(R5_q), .clk(clk), .clr(clr));
  Register #(.width(32)) R4 (.D(WD3), .en(decoder_1_out4), .Q(R4_q), .clk(clk), .clr(clr));
  Register #(.width(32)) R3 (.D(WD3), .en(decoder_1_out3), .Q(R3_q), .clk(clk), .clr(clr));
  Register #(.width(32)) R2 (.D(WD3), .en(decoder_1_out2), .Q(R2_q), .clk(clk), .clr(clr));
  Register #(.width(32)) R1 (.D(WD3), .en(decoder_1_out1), .Q(R1_q), .clk(clk), .clr(clr));
  Register #(.width(32)) R0 (.D(WD3), .en(decoder_1_out0), .Q(R0_q), .clk(clk), .clr(clr));
  Multiplexer #(.select(4), .width(32), .enable("false")) multiplexer_1 (
    .in0(R0_q), .in1(R1_q), .in2(R2_q), .in3(R3_q), .in4(R4_q), .in5(R5_q), .in6(R6_q), .in7(R7_q),
    .in8(R8_q), .in9(R9_q), .in10(R10_q), .in11(R11_q), .in12(R12_q), .in13(R13_q), .in14(R14_q), .in15(R15),
    .out(RD1), .sel(A1));
  Multiplexer #(.select(4), .width(32), .enable("false")) multiplexer_2 (
    .in0(R0_q), .in1(R1_q), .in2(R2_q), .in3(R3_q), .in4(R4_q), .in5(R5_q), .in6(R6_q), .in7(R7_q),
    .in8(R8_q), .in9(R9_q), .in10(R10_q), .in11(R11_q), .in12(R12_q), .in13(R13_q), .in14(R14_q), .out(RD2),
    .sel(A2));  // open: in15
endmodule
