// Logisim project main_decoder.circ as structural Verilog: 8 circuits, main circuit main
module main (
  input  [1:0] op,
  input  f0,
  input  f5,
  output Branch,
  output MemtoReg,
  output MemW,
  output ALUSrc,
  output [1:0] ImmSrc,
  output RegW,
  output [1:0] RegSrc,
  output ALUOp
);

  MemW_encoder memw_encoder_1 (.op(op), .f0(f0), .MemW(MemW));
  ALUSrc_encoder alusrc_encoder_1 (.op(op), .f5(f5), .ALUSrc(ALUSrc));
  RegW_encoder regw_encoder_1 (.op(op), .f0(f0), .RegW(RegW));
  RegSrc_encoder regsrc_encoder_1 (.op(op), .RegSrc(RegSrc), .f5(f5));
  ALUOp_encoder aluop_encoder_1 (.op(op), .ALUOp(ALUOp));
  MemtoReg_encoder memtoreg_encoder_1 (.op(op), .out_2(MemtoReg));

  assign Branch = op[1];
  assign ImmSrc = op;
endmodule

module ALUSrc_encoder (
  input  [1:0] op,
  input  f5,
  output ALUSrc
);

  wire and_1_out, and_2_out, and_3_out;

  and and_1 (and_1_out, ~op[1], ~op[0], f5);  // AND_Gate
  and and_2 (and_2_out, ~op[1], ~f5, op[0]);  // AND_Gate
  and and_3 (and_3_out, op[1], ~op[0]);  // AND_Gate
  or or_1 (ALUSrc, and_1_out, and_2_out, and_3_out);
endmodule

module RegW_encoder (
  input  [1:0] op,
  input  f0,
  output RegW
);

  wire and_1_out, and_2_out;

  and and_1 (and_1_out, ~op[1], ~op[0]);  // AND_Gate
  and and_2 (and_2_out, ~op[1], op[0], f0);  // AND_Gate
  or or_1 (RegW, and_1_out, and_2_out);
endmodule

module ALUOp_encoder (
  input  [1:0] op,
  output ALUOp
);

  and and_1 (ALUOp, ~op[1], ~op[0]);  // AND_Gate
endmodule

module Branch_encoder (
  input  [1:0] op,
  output Branch
);

  and and_1 (Branch, op[1], ~op[0]);  // AND_Gate
endmodule

module MemtoReg_encoder (
  input  [1:0] op,
  output out_2
);

  and and_1 (out_2, ~op[1], op[0]);  // AND_Gate
endmodule

module MemW_encoder (
  input  [1:0] op,
  input  f0,
  output MemW
);

  and and_1 (MemW, ~op[1], op[0], ~f0);  // AND_Gate
endmodule

module RegSrc_encoder (
  input  [1:0] op,
  input  f5,
  output [1:0] RegSrc
);

  wire and_1_out, and_2_out, and_3_out;

  and and_1 (and_1_out, ~op[1], ~op[0], f5);  // AND_Gate
  and and_2 (and_2_out, ~op[1], ~f5, op[0]);  // AND_Gate
  and and_3 (and_3_out, op[1], ~op[0]);  // AND_Gate
  or or_1 (RegSrc[1], and_1_out, and_2_out, and_3_out);

  assign RegSrc[0] = op[1];
endmodule
