// Logisim project single_cycle_cpu.circ as structural Verilog: 5 circuits, main circuit main
module main (
);

  wire alusrct, clear_out, clkt, main_1_memtoreg, main_1_pcsrc, main_1_regwrite, memwt, reset_out;
  wire [1:0] aluctrlt, immsrct, main_1_regsrc1_0, opt;
  wire [3:0] aluft, condt, instsplitter_1_x4_0_3, instsplitter_1_x4_15_12, instsplitter_1_x4_15_12_2,
       instsplitter_1_x4_16_19, multiplexer_2_out, multiplexer_3_out;
  wire [5:0] funct;
  wire [7:0] n32_8_adapter_1__8_0, n32_8_adapter_2__8_0;
  wire [23:0] instsplitter_1_x24_23_0;
  wire [31:0] adder_1_out, adder_2_out, datat, extend_1_x32, multiplexer_1_out, multiplexer_4_out,
       multiplexer_5_out, multiplexer_6_out, PC_q, ram_1_data, registerfile_1_rd1, rom_1_data, shifter_1_out,
       undriven;

  Clock #(.highDuration(2)) clock_1 (.out(clkt));
  Multiplexer #(.width(32), .enable("false")) multiplexer_1 (
    .in0(adder_1_out), .in1(multiplexer_6_out), .out(multiplexer_1_out), .sel(main_1_pcsrc));
  Register #(.width(32)) PC (.D(multiplexer_1_out), .Q(PC_q), .clk(clkt), .clr(reset_out));  // open: en
  Button reset (.out(reset_out));
  _32_8_adapter u_32_8_adapter_1 (._32_0(PC_q), ._8_0(n32_8_adapter_1__8_0));
  Adder #(.width(32)) adder_1 (.a(PC_q), .b(32'h4), .out(adder_1_out));  // open: cin, cout
  InstSplitter instsplitter_1 (
    .RD_x32(rom_1_data), .x4_0_3(instsplitter_1_x4_0_3), .x24_23_0(instsplitter_1_x24_23_0),
    .x4_31_28(condt), .x2_27_26(opt), .x6_25_20(funct), .x4_16_19(instsplitter_1_x4_16_19),
    .x4_15_12(instsplitter_1_x4_15_12), .x4_15_12_2(instsplitter_1_x4_15_12_2));
  ROM #(.dataWidth(32)) rom_1 (.addr(n32_8_adapter_1__8_0), .data(rom_1_data));  // open: sel
  Multiplexer #(.width(4), .enable("false")) multiplexer_2 (
    .in0(instsplitter_1_x4_16_19), .in1(4'b1111), .out(multiplexer_2_out), .sel(main_1_regsrc1_0[0]));
  Adder #(.width(32)) adder_2 (.a(adder_1_out), .b(32'h4), .out(adder_2_out));  // open: cin, cout
  control_unit_main main_1 (
    .clk(clkt), .Rd3_0(instsplitter_1_x4_15_12_2), .Op(opt), .Funct5_0(funct), .Cond3_0(condt),
    .ALUFlags3_0(aluft), .PCSrc(main_1_pcsrc), .RegWrite(main_1_regwrite), .MemtoReg(main_1_memtoreg),
    .MemWrite(memwt), .ALUSrc(alusrct), .ImmSrc1_0(immsrct), .RegSrc1_0(main_1_regsrc1_0),
    .ALUControl1_0(aluctrlt));
  Multiplexer #(.width(4), .enable("false")) multiplexer_3 (
    .in0(instsplitter_1_x4_0_3), .in1(instsplitter_1_x4_15_12), .out(multiplexer_3_out),
    .sel(main_1_regsrc1_0[1]));
  Button clear (.out(clear_out));
  RegisterFile registerfile_1 (
    .WD3(multiplexer_6_out), .clr(clear_out), .A1(multiplexer_2_out), .A2(multiplexer_3_out),
    .A3(instsplitter_1_x4_15_12), .RD1(registerfile_1_rd1), .RD2(datat), .WE3(main_1_regwrite), .clk(clkt),
    .R15(adder_2_out));
  Extend extend_1 (.x24(instsplitter_1_x24_23_0), .ImmSrc(immsrct), .x32(extend_1_x32));
  Multiplexer #(.width(32), .enable("false")) multiplexer_4 (
    .in0(extend_1_x32), .in1(shifter_1_out), .out(multiplexer_4_out), .sel(opt[1]));
  Multiplexer #(.width(32), .enable("false")) multiplexer_5 (
    .in0(datat), .in1(multiplexer_4_out), .out(multiplexer_5_out), .sel(alusrct));
  Shifter #(.width(32)) shifter_1 (.in(extend_1_x32), .\dist (5'b00010), .out(shifter_1_out));
  // Probe on aluft
  ALU alu_1 (
    .ALUControl(aluctrlt), .ALU_Flags(aluft), .A(registerfile_1_rd1), .B(multiplexer_5_out),
    .ALU_Result(undriven));
  _32_8_adapter u_32_8_adapter_2 (._32_0(undriven), ._8_0(n32_8_adapter_2__8_0));
  RAM #(.dataWidth(32), .bus("separate")) ram_1 (
    .addr(n32_8_adapter_2__8_0), .din(datat), .data(ram_1_data), .str(memwt), .clk(clkt));  // open: sel, ld, clr
  Multiplexer #(.width(32), .enable("false")) multiplexer_6 (
    .in0(undriven), .in1(ram_1_data), .out(multiplexer_6_out), .sel(main_1_memtoreg));

  // Notes on the sheet:
  //   contents of rom_1 (hex, n*v repeats v):
  //   e2813002 0 0 0 e0411001 0 0 0 e0433003 0 0 0 e280000a 0 0 0 e2811007 0 0 0 e0402001 0 0 0 e2123000 0
  //   0 0 104001 0 0 0 13805005 0 0 0 e0400000 0 0 0 e0411001 0 0 0 e0422002 0 0 0 e0433003 0 0 0 e0444004
  //   0 0 0 e0455005 0 0 0 e2800008 0 0 0 e2901009 0 0 0 c2412003 0 0 0 b2412002 0 0 0 e5802004 0 0 0
  //   e2833004 0 0 0 e7904003 0 0 0 e254500f 0 0 0 b0856004 0 0 0 e0400000 0 0 0 e0411001 0 0 0 e0422002 0
  //   0 0 e0433003 0 0 0 e0444004 0 0 0 e0455005 0 0 0 e0466006 0 0 0 e2800050 0 0 0 e2811025 0 0 0
  //   e2833075 0 0 0 10811000 0 0 0 c0433000 0 0 0 e0036004 0 0 0 e1807001 0 0 0 e0400000 0 0 0 e0411001 0
  //   0 0 e0433003 0 0 0 e0444004 0 0 0 e0466006 0 0 0 e0477007 0 0 0 e2801000 0 0 0 e2805005 0 0 0
  //   e2555000 0 0 0 a000002 0 0 0 e2811001 0 0 0 e2455001 0 0 0 1afffffa 0 0 0 e0411001 0 0 0 e0455005 0
  //   0 0 e28000d2 0 0 0 e281101e 0 0 0 e2833000 0 0 0 e0500001 0 0 0 ba000001 0 0 0 e2833001 0 0 0
  //   eafffffb 0 0 0 eafffffe
  //   AluResult
  //   ReadData
  //   Result
endmodule

module _32_8_adapter (
  input  [31:0] _32_0,
  output [7:0] _8_0
);


  assign _8_0 = _32_0[7:0];
endmodule

module InstSplitter (
  input  [31:0] RD_x32,
  output [23:0] x24_23_0,
  output [3:0] x4_0_3,
  output [3:0] x4_15_12,
  output [3:0] x4_15_12_2,
  output [3:0] x4_31_28,
  output [1:0] x2_27_26,
  output [5:0] x6_25_20,
  output [3:0] x4_16_19
);


  assign x2_27_26 = RD_x32[27:26];
  assign x4_0_3 = RD_x32[3:0];
  assign x4_15_12 = RD_x32[15:12];
  assign x4_15_12_2 = RD_x32[15:12];
  assign x4_16_19 = RD_x32[19:16];
  assign x4_31_28 = RD_x32[31:28];
  assign x6_25_20 = RD_x32[25:20];
  assign x24_23_0 = RD_x32[23:0];

  // Notes on the sheet:
  //   (20-23)
  //   24-25
endmodule

module register_file_a (
  input  [31:0] WD3,
  input  clk,
  input  [3:0] A1,
  input  WE3,
  input  [3:0] A3,
  input  [3:0] A2,
  input  [31:0] R15,
  output [31:0] RD1,
  output [31:0] RD2
);

  wire demultiplexer_1_out0, demultiplexer_1_out1, demultiplexer_1_out2, demultiplexer_1_out3,
       demultiplexer_1_out4, demultiplexer_1_out5, demultiplexer_1_out6, demultiplexer_1_out7,
       demultiplexer_1_out8, demultiplexer_1_out9, demultiplexer_1_out10, demultiplexer_1_out11,
       demultiplexer_1_out12, demultiplexer_1_out13, demultiplexer_1_out14, demultiplexer_1_out15;
  wire [31:0] R0_q, R1_q, R2_q, R3_q, R4_q, R5_q, R6_q, R7_q, R8_q, R9_q, R10_q, R11_q, R12_q, R13_q, R14_q;

  Demultiplexer #(.select(4)) demultiplexer_1 (
    .out0(demultiplexer_1_out0), .out1(demultiplexer_1_out1), .out2(demultiplexer_1_out2),
    .out3(demultiplexer_1_out3), .out4(demultiplexer_1_out4), .out5(demultiplexer_1_out5),
    .out6(demultiplexer_1_out6), .out7(demultiplexer_1_out7), .out8(demultiplexer_1_out8),
    .out9(demultiplexer_1_out9), .out10(demultiplexer_1_out10), .out11(demultiplexer_1_out11),
    .out12(demultiplexer_1_out12), .out13(demultiplexer_1_out13), .out14(demultiplexer_1_out14),
    .out15(demultiplexer_1_out15), .in(WE3), .sel(A3));  // open: en
  Register #(.width(32)) R0 (.D(WD3), .en(demultiplexer_1_out0), .Q(R0_q), .clk(clk));  // open: clr
  Register #(.width(32)) R4 (.D(WD3), .en(demultiplexer_1_out4), .Q(R4_q), .clk(clk));  // open: clr
  Register #(.width(32)) R8 (.D(WD3), .en(demultiplexer_1_out8), .Q(R8_q), .clk(clk));  // open: clr
  Register #(.width(32)) R12 (.D(WD3), .en(demultiplexer_1_out12), .Q(R12_q), .clk(clk));  // open: clr
  Register #(.width(32)) R1 (.D(WD3), .en(demultiplexer_1_out1), .Q(R1_q), .clk(clk));  // open: clr
  Register #(.width(32)) R5 (.D(WD3), .en(demultiplexer_1_out5), .Q(R5_q), .clk(clk));  // open: clr
  Register #(.width(32)) R9 (.D(WD3), .en(demultiplexer_1_out9), .Q(R9_q), .clk(clk));  // open: clr
  Register #(.width(32)) R13 (.D(WD3), .en(demultiplexer_1_out13), .Q(R13_q), .clk(clk));  // open: clr
  Register #(.width(32)) R10 (.D(WD3), .en(demultiplexer_1_out10), .Q(R10_q), .clk(clk));  // open: clr
  Register #(.width(32)) R14 (.D(WD3), .en(demultiplexer_1_out14), .Q(R14_q), .clk(clk));  // open: clr
  Register #(.width(32)) R2 (.D(WD3), .en(demultiplexer_1_out2), .Q(R2_q), .clk(clk));  // open: clr
  Register #(.width(32)) R6 (.D(WD3), .en(demultiplexer_1_out6), .Q(R6_q), .clk(clk));  // open: clr
  Register #(.width(32)) R3 (.D(WD3), .en(demultiplexer_1_out3), .Q(R3_q), .clk(clk));  // open: clr
  Register #(.width(32)) R7 (.D(WD3), .en(demultiplexer_1_out7), .Q(R7_q), .clk(clk));  // open: clr
  Register #(.width(32)) R11 (.D(WD3), .en(demultiplexer_1_out11), .Q(R11_q), .clk(clk));  // open: clr
  Register #(.width(32)) u_R15 (.D(WD3), .en(demultiplexer_1_out15), .clk(clk));  // open: Q, clr
  Multiplexer #(.select(4), .width(32), .enable("false")) multiplexer_1 (
    .in0(R0_q), .in1(R1_q), .in2(R2_q), .in3(R3_q), .in4(R4_q), .in5(R5_q), .in6(R6_q), .in7(R7_q),
    .in8(R8_q), .in9(R9_q), .in10(R10_q), .in11(R11_q), .in12(R12_q), .in13(R13_q), .in14(R14_q), .in15(R15),
    .out(RD1), .sel(A1));
  Multiplexer #(.select(4), .width(32), .enable("false")) multiplexer_2 (
    .in0(R0_q), .in1(R1_q), .in2(R2_q), .in3(R3_q), .in4(R4_q), .in5(R5_q), .in6(R6_q), .in7(R7_q),
    .in8(R8_q), .in9(R9_q), .in10(R10_q), .in11(R11_q), .in12(R12_q), .in13(R13_q), .in14(R14_q), .in15(R15),
    .out(RD2), .sel(A2));

  // Other names for the same wires on the sheet: clkt = clk; WD3T[31:0] = WD3
endmodule

module Extend (
  input  [23:0] x24,
  input  [1:0] ImmSrc,
  output [31:0] x32
);

  wire [31:0] bit_extender_1_out, bit_extender_2_out, bit_extender_3_out;

  assign bit_extender_1_out = {{24{1'b0}}, x24[7:0]};  // Bit_Extender bit_extender_1
  assign bit_extender_2_out = {{20{1'b0}}, x24[11:0]};  // Bit_Extender bit_extender_2
  assign bit_extender_3_out = {{8{x24[23]}}, x24};  // Bit_Extender bit_extender_3
  Multiplexer #(.select(2), .width(32), .enable("false")) multiplexer_1 (
    .in0(bit_extender_1_out), .in1(bit_extender_2_out), .in2(bit_extender_3_out), .in3(bit_extender_3_out),
    .out(x32), .sel(ImmSrc));
endmodule
